# Fritzing sketch chimarrao (saved by Fritzing 0.9.3b)
circuit board: 8.46667cm x 5.64444cm
breadboards: 1

parts:
  Bauteil1 = Arduino Nano (Rev3.0)
  DS1 = DS18B20 1-Wire Temperature Sensor [part_number=DS18B20]
  LED1 = smd LED [color="Red (633nm)" package="0805 [SMD]"]
  LED2 = smd LED [color="Red (633nm)" package="0805 [SMD]"]
  LED3 = smd LED [color="Green (570nm)" package="0805 [SMD]"]
  R2 = Resistor [tolerance=±5% resistance=150 package="0603 [SMD]"]
  R3 = Resistor [tolerance=±5% resistance=150 package="0603 [SMD]"]
  J1 = Piezo Speaker
  R1 = Resistor [tolerance=±5% resistance=150 package="0603 [SMD]"]
  S1 = Toggle Switch [package=THT]
  VCC1 = 4 x AAA Battery Mount

nets:
  N1: Bauteil1.GND, R2.Pin_0, R3.Pin_0, J1.pin1, R1.Pin_0, VCC1.-
  N2: Bauteil1.D2, J1.pin2
  N3: Bauteil1.D3, LED2.anode
  N4: Bauteil1.D4, LED1.anode
  N5: Bauteil1.D5, LED3.anode
  N6: Bauteil1.VIN, S1.COM
  N7: Bauteil1.A3, DS1.DQ
  3V3: Bauteil1.3V3, DS1.VDD
  N8: LED1.cathode, R2.Pin_1
  N9: LED2.cathode, R1.Pin_1
  N10: LED3.cathode, R3.Pin_1
  N11: S1.L2, VCC1.+
